// Digital circuit soc.dig as structural Verilog
module soc (
  input  clk,
  output [31:0] x10
);

  cpu #(.applicationType("IVERILOG"), .iverilogOptions("-I C:/Users/mirac/Documents/fpga/femtoriscv"), .CodeFile("cpu.v")) u_cpu (
    .clk(clk), .resetn(1'b1), .x10(x10));

  // Notes on the sheet:
  //   clk: Hz: 10
endmodule
